// Logisim project 4bit parallel adder and subtractor.circ as structural Verilog: 1 circuit, main circuit main
module main (
  input  CARRY,
  input  [3:0] A,
  input  [3:0] B,
  input  K,
  output [3:0] SUM_SUB,
  output CARRYOUT
);

  wire main_1_p5, main_2_p5, main_3_p5, xor_1_out, xor_2_out, xor_3_out, xor_4_out;

  xor xor_1 (xor_1_out, B[0], K);
  xor xor_2 (xor_2_out, B[1], K);
  xor xor_3 (xor_3_out, B[2], K);
  xor xor_4 (xor_4_out, B[3], K);
  // FULL_ADDDEr_main main_1: pin names not known; wires that end beside it: A[0], xor_1_out, CARRY, SUM_SUB[0], main_1_p5
  // FULL_ADDDEr_main main_2: pin names not known; wires that end beside it: A[1], xor_2_out, main_1_p5, SUM_SUB[1], main_2_p5
  // FULL_ADDDEr_main main_3: pin names not known; wires that end beside it: A[2], xor_3_out, main_2_p5, SUM_SUB[2], main_3_p5
  // FULL_ADDDEr_main main_4: pin names not known; wires that end beside it: A[3], xor_4_out, main_3_p5, SUM_SUB[3], CARRYOUT
endmodule
