// Logisim project masterfile.circ as structural Verilog
module FA (
  input  A,
  input  B,
  input  C,
  output S,
  output C_2
);

  wire and_1_out, and_2_out, and_3_out, and_4_out, and_5_out, and_6_out, and_7_out, not_1_out, not_2_out,
       not_3_out, not_4_out, not_5_out, not_6_out;

  not not_1 (not_1_out, A);
  not not_2 (not_2_out, B);
  not not_3 (not_3_out, A);
  not not_4 (not_4_out, C);
  not not_5 (not_5_out, B);
  not not_6 (not_6_out, C);
  and and_1 (and_1_out, B, C);
  and and_2 (and_2_out, A, C);
  and and_3 (and_3_out, A, B);
  and and_4 (and_4_out, not_1_out, not_2_out, C);
  and and_5 (and_5_out, not_3_out, B, not_4_out);
  and and_6 (and_6_out, A, not_5_out, not_6_out);
  and and_7 (and_7_out, A, B, C);
  or or_1 (C_2, and_1_out, and_2_out, and_3_out);
  or or_2 (S, and_4_out, and_5_out, and_6_out, and_7_out);
endmodule

module PARALLEL_FA (
  input  in_1,
  input  [3:0] in_2,
  input  [3:0] in_3,
  output [3:0] out_4
);

  wire fa_1_c_2, fa_2_c_2, fa_3_c_2;

  FA fa_1 (.A(in_2[0]), .B(in_3[0]), .C(in_1), .S(out_4[0]), .C_2(fa_1_c_2));
  FA fa_2 (.A(in_2[1]), .B(in_3[1]), .C(fa_1_c_2), .S(out_4[1]), .C_2(fa_2_c_2));
  FA fa_3 (.A(in_2[2]), .B(in_3[2]), .C(fa_2_c_2), .S(out_4[2]), .C_2(fa_3_c_2));
  FA fa_4 (.A(in_2[3]), .B(in_3[3]), .C(fa_3_c_2), .S(out_4[3]));  // open: C_2
endmodule

module MUX (
  input  A,
  input  B,
  input  C,
  input  D,
  input  S1,
  input  S2,
  output Y
);

  wire and_1_out, and_2_out, and_3_out, and_4_out, not_1_out, not_2_out, not_3_out, not_4_out;

  not not_1 (not_1_out, S1);
  not not_2 (not_2_out, S2);
  not not_3 (not_3_out, S1);
  not not_4 (not_4_out, S2);
  and and_1 (and_1_out, not_1_out, not_2_out, A);
  and and_2 (and_2_out, not_3_out, S2, B);
  and and_3 (and_3_out, S1, not_4_out, C);
  and and_4 (and_4_out, S1, S2, D);
  or or_1 (Y, and_1_out, and_2_out, and_3_out, and_4_out);
endmodule

module _1BIT_AU (
  input  in_1,
  input  in_2,
  input  in_3,
  input  in_4,
  input  in_5,
  input  in_6,
  output out_7,
  output out_8
);

  wire mux_1_y, not_1_out, not_2_out;

  not not_1 (not_1_out, in_2);
  not not_2 (not_2_out, in_4);
  MUX mux_1 (.A(in_2), .B(not_1_out), .C(in_4), .D(not_2_out), .S1(in_5), .S2(in_6), .Y(mux_1_y));
  FA fa_1 (.A(in_3), .B(in_1), .C(mux_1_y), .S(out_7), .C_2(out_8));
endmodule

module _1_BIT_LU (
  input  in_1,
  input  in_2,
  input  in_3,
  input  in_4,
  output out_5
);

  wire and_1_out, not_1_out, or_1_out, xor_1_out;

  and and_1 (and_1_out, in_1, in_2);
  or or_1 (or_1_out, in_1, in_2);
  xor xor_1 (xor_1_out, in_1, in_2);
  not not_1 (not_1_out, in_1);
  MUX mux_1 (.A(and_1_out), .B(or_1_out), .C(xor_1_out), .D(not_1_out), .S1(in_3), .S2(in_4), .Y(out_5));
endmodule

module _2_BIT_MUX (
  input  A,
  input  B,
  input  S1,
  output Y
);

  wire and_1_out, and_2_out, not_1_out;

  not not_1 (not_1_out, S1);
  and and_1 (and_1_out, not_1_out, A);
  and and_2 (and_2_out, S1, B);
  or or_1 (Y, and_1_out, and_2_out);
endmodule

module _1_BIT_ALU (
  input  in_1,
  input  in_2,
  input  in_3,
  input  in_4,
  input  in_5,
  input  in_6,
  input  in_7,
  output out_8,
  output out_9
);

  wire n1_bit_lu_1_out_5, n1bit_au_1_out_7;

  _1BIT_AU u_1bit_au_1 (
    .in_1(in_1), .in_2(in_2), .in_3(in_3), .in_4(in_4), .in_5(in_5), .in_6(in_6), .out_7(n1bit_au_1_out_7),
    .out_8(out_9));
  _1_BIT_LU u_1_bit_lu_1 (.in_1(in_1), .in_2(in_2), .in_3(in_5), .in_4(in_6), .out_5(n1_bit_lu_1_out_5));
  _2_BIT_MUX u_2_bit_mux_1 (.A(n1bit_au_1_out_7), .B(n1_bit_lu_1_out_5), .S1(in_7), .Y(out_8));
endmodule

module _4_BIT_AU (
  input  in_1,
  input  [3:0] in_2,
  input  [3:0] in_3,
  input  [3:0] in_4,
  input  in_5,
  input  in_6,
  output [3:0] out_7,
  output out_8
);

  wire n1bit_au_1_out_8, n1bit_au_2_out_8, n1bit_au_3_out_8, n1bit_au_4_out_8;

  _1BIT_AU u_1bit_au_1 (
    .in_1(in_2[0]), .in_2(in_3[0]), .in_3(in_1), .in_4(in_4[0]), .in_5(in_5), .in_6(in_6), .out_7(out_7[0]),
    .out_8(n1bit_au_1_out_8));
  _1BIT_AU u_1bit_au_2 (
    .in_1(in_2[1]), .in_2(in_3[1]), .in_3(n1bit_au_1_out_8), .in_4(in_4[1]), .in_5(in_5), .in_6(in_6),
    .out_7(out_7[1]), .out_8(n1bit_au_2_out_8));
  _1BIT_AU u_1bit_au_3 (
    .in_1(in_2[2]), .in_2(in_3[2]), .in_3(n1bit_au_2_out_8), .in_4(in_4[2]), .in_5(in_5), .in_6(in_6),
    .out_7(out_7[2]), .out_8(n1bit_au_3_out_8));
  _1BIT_AU u_1bit_au_4 (
    .in_1(in_2[3]), .in_2(in_2[3]), .in_3(n1bit_au_3_out_8), .in_4(in_4[3]), .in_5(in_5), .in_6(in_6),
    .out_7(out_7[3]), .out_8(n1bit_au_4_out_8));
  or or_1 (out_8, n1bit_au_3_out_8, n1bit_au_4_out_8);

  assign in_3[3] = in_2[3];
endmodule

module _4_BIT_LU (
  input  [3:0] in_1,
  input  [3:0] in_2,
  input  in_3,
  input  in_4,
  output [3:0] out_5
);

  _1_BIT_LU u_1_bit_lu_1 (.in_1(in_1[0]), .in_2(in_2[0]), .in_3(in_3), .in_4(in_3), .out_5(out_5[0]));
  _1_BIT_LU u_1_bit_lu_2 (.in_1(in_1[1]), .in_2(in_2[1]), .in_3(in_3), .in_4(in_3), .out_5(out_5[1]));
  _1_BIT_LU u_1_bit_lu_3 (.in_1(in_1[2]), .in_2(in_2[2]), .in_3(in_3), .in_4(in_3), .out_5(out_5[2]));
  _1_BIT_LU u_1_bit_lu_4 (.in_1(in_1[3]), .in_2(in_1[3]), .in_3(in_3), .in_4(in_3), .out_5(out_5[3]));

  assign in_2[3] = in_1[3];
  assign in_4 = in_3;
endmodule

module _4_BIT_ALU (
  input  in_1,
  input  [3:0] in_2,
  input  [3:0] in_3,
  input  [3:0] in_4,
  input  in_5,
  input  in_6,
  input  in_7,
  output [3:0] out_8
);

  wire [3:0] n4_bit_au_1_out_7, n4_bit_lu_1_out_5;

  _4_BIT_AU u_4_bit_au_1 (
    .in_1(in_1), .in_2(in_2), .in_3(in_3), .in_4(in_4), .in_5(in_5), .in_6(in_6), .out_7(n4_bit_au_1_out_7));  // open: out_8
  _4_BIT_LU u_4_bit_lu_1 (.in_1(in_2), .in_2(in_3), .in_3(in_5), .in_4(in_6), .out_5(n4_bit_lu_1_out_5));
  _4_BIT_2_1_MUX u_4_bit_2_1_mux_1 (.in_1(n4_bit_au_1_out_7), .in_2(n4_bit_lu_1_out_5), .in_3(in_7), .out_4(out_8));
endmodule

module _4_BIT_2_1_MUX (
  input  [3:0] in_1,
  input  [3:0] in_2,
  input  in_3,
  output [3:0] out_4
);

  _2_BIT_MUX u_2_bit_mux_1 (.A(in_1[0]), .B(in_2[0]), .S1(in_3), .Y(out_4[0]));
  _2_BIT_MUX u_2_bit_mux_2 (.A(in_1[1]), .B(in_2[1]), .S1(in_3), .Y(out_4[1]));
  _2_BIT_MUX u_2_bit_mux_3 (.A(in_1[2]), .B(in_2[2]), .S1(in_3), .Y(out_4[2]));
  _2_BIT_MUX u_2_bit_mux_4 (.A(in_1[3]), .B(in_2[3]), .S1(in_3), .Y(out_4[3]));
endmodule

module register_file (
  input  [3:0] in_1,
  input  in_2,
  input  in_3,
  input  in_4,
  input  [1:0] in_5,
  input  in_6,
  input  in_7,
  output [3:0] out_8,
  output [3:0] out_9
);

  wire and_1_out, and_2_out, and_3_out, and_4_out, clock_1_out, decoder_1_out0, decoder_1_out1,
       decoder_1_out2, decoder_1_out3;
  wire [3:0] register_1_q, register_2_q, register_3_q, register_4_q;

  Decoder #(.select(2), .enable("false")) decoder_1 (
    .out0(decoder_1_out0), .out1(decoder_1_out1), .out2(decoder_1_out2), .out3(decoder_1_out3), .sel(in_5));
  Clock clock_1 (.out(clock_1_out));
  Register #(.width(4)) register_1 (.D(in_1), .en(and_1_out), .Q(register_1_q), .clk(clock_1_out));  // open: clr
  and and_1 (and_1_out, in_2, decoder_1_out0);
  Register #(.width(4)) register_2 (.D(in_1), .en(and_2_out), .Q(register_2_q), .clk(clock_1_out));  // open: clr
  and and_2 (and_2_out, in_2, decoder_1_out1);
  Register #(.width(4)) register_3 (.D(in_1), .en(and_3_out), .Q(register_3_q), .clk(clock_1_out));  // open: clr
  and and_3 (and_3_out, in_2, decoder_1_out2);
  Register #(.width(4)) register_4 (.D(in_1), .en(and_4_out), .Q(register_4_q), .clk(clock_1_out));  // open: clr
  and and_4 (and_4_out, in_2, decoder_1_out3);
  _4_bit_4_1_mux u_4_bit_4_1_mux_1 (
    .in_1(register_1_q), .in_2(register_2_q), .in_3(register_3_q), .in_4(register_4_q), .in_5(in_3),
    .in_6(in_4), .out_7(out_8));
  _4_bit_4_1_mux u_4_bit_4_1_mux_2 (
    .in_1(register_1_q), .in_2(register_2_q), .in_3(register_3_q), .in_4(register_4_q), .in_5(in_6),
    .in_6(in_7), .out_7(out_9));
endmodule

module _4_bit_4_1_mux (
  input  [3:0] in_1,
  input  [3:0] in_2,
  input  [3:0] in_3,
  input  [3:0] in_4,
  input  in_5,
  input  in_6,
  output [3:0] out_7
);

  MUX mux_1 (.A(in_1[0]), .B(in_2[0]), .C(in_3[0]), .D(in_4[0]), .S1(in_5), .S2(in_6), .Y(out_7[0]));
  MUX mux_2 (.A(in_1[1]), .B(in_2[1]), .C(in_3[1]), .D(in_4[1]), .S1(in_5), .S2(in_6), .Y(out_7[1]));
  MUX mux_3 (.A(in_1[2]), .B(in_2[2]), .C(in_3[2]), .D(in_4[2]), .S1(in_5), .S2(in_6), .Y(out_7[2]));
  MUX mux_4 (.A(in_1[3]), .B(in_2[3]), .C(in_3[3]), .D(in_4[3]), .S1(in_5), .S2(in_6), .Y(out_7[3]));
endmodule

module register___alu (
  input  [3:0] in_1,
  input  in_2,
  input  in_3,
  input  in_4,
  input  in_5,
  input  [1:0] in_6,
  input  [3:0] in_7,
  input  in_8,
  input  in_9,
  input  in_10,
  input  in_11,
  input  in_12,
  output [3:0] out_13,
  output [3:0] out_14,
  output [3:0] out_15
);

  wire and_1_out, and_2_out, and_3_out, and_4_out, clock_1_out, decoder_1_out0, decoder_1_out1,
       decoder_1_out2, decoder_1_out3;
  wire [3:0] register_1_q, register_2_q, register_3_q, register_4_q;

  Decoder #(.select(2), .enable("false")) decoder_1 (
    .out0(decoder_1_out0), .out1(decoder_1_out1), .out2(decoder_1_out2), .out3(decoder_1_out3), .sel(in_6));
  Clock clock_1 (.out(clock_1_out));
  Register #(.width(4)) register_1 (.D(in_1), .en(and_1_out), .Q(register_1_q), .clk(clock_1_out));  // open: clr
  and and_1 (and_1_out, in_2, decoder_1_out0);
  Register #(.width(4)) register_2 (.D(in_1), .en(and_2_out), .Q(register_2_q), .clk(clock_1_out));  // open: clr
  and and_2 (and_2_out, in_2, decoder_1_out1);
  Register #(.width(4)) register_3 (.D(in_1), .en(and_3_out), .Q(register_3_q), .clk(clock_1_out));  // open: clr
  and and_3 (and_3_out, in_2, decoder_1_out2);
  Register #(.width(4)) register_4 (.D(in_1), .en(and_4_out), .Q(register_4_q), .clk(clock_1_out));  // open: clr
  and and_4 (and_4_out, in_2, decoder_1_out3);
  _4_bit_4_1_mux u_4_bit_4_1_mux_1 (
    .in_1(register_1_q), .in_2(register_2_q), .in_3(register_3_q), .in_4(register_4_q), .in_5(in_4),
    .in_6(in_5), .out_7(out_13));
  _4_bit_4_1_mux u_4_bit_4_1_mux_2 (
    .in_1(register_1_q), .in_2(register_2_q), .in_3(register_3_q), .in_4(register_4_q), .in_5(in_9),
    .in_6(in_11), .out_7(out_15));
  _4_BIT_ALU u_4_bit_alu_1 (
    .in_1(in_3), .in_2(out_13), .in_3(out_15), .in_4(in_7), .in_5(in_8), .in_6(in_10), .in_7(in_12),
    .out_8(out_14));
endmodule

module logic_gates_using_mux (
  input  in_1,
  input  in_2,
  input  in_3,
  input  in_4,
  input  in_5,
  input  \not ,
  input  in_7,
  input  in_8,
  input  in_9,
  input  \and ,
  input  in_11,
  input  in_12,
  input  in_13,
  input  in_14,
  input  in_15,
  input  \or ,
  input  \xor ,
  output out_18,
  output out_19,
  output out_20,
  output out_21
);

  MUX mux_1 (.A(in_9), .B(in_11), .C(in_11), .D(in_13), .S1(in_15), .S2(\xor ), .Y(out_21));
  MUX mux_2 (.A(in_2), .B(in_2), .C(in_2), .D(in_5), .S1(in_7), .S2(\and ), .Y(out_19));
  MUX mux_3 (.A(in_8), .B(in_12), .C(in_12), .D(in_12), .S1(in_14), .S2(\or ), .Y(out_20));
  MUX mux_4 (.A(in_1), .B(in_1), .C(in_3), .D(in_3), .S1(in_4), .S2(\not ), .Y(out_18));
endmodule

module fourbitparallel_adder_and_substractor (
  input  in_1,
  input  [3:0] A,
  input  [3:0] B,
  input  K,
  output [3:0] SUM_SUB,
  output CARRYOUT
);

  wire adder_1_cout, adder_2_cout, adder_3_cout, xor_1_out, xor_2_out, xor_3_out, xor_4_out;

  xor xor_1 (xor_1_out, B[0], K);
  xor xor_2 (xor_2_out, B[1], K);
  xor xor_3 (xor_3_out, B[2], K);
  xor xor_4 (xor_4_out, B[3], K);
  Adder #(.width(1)) adder_1 (.a(xor_1_out), .b(A[0]), .out(SUM_SUB[0]), .cin(in_1), .cout(adder_1_cout));
  Adder #(.width(1)) adder_2 (.a(xor_2_out), .b(A[1]), .out(SUM_SUB[1]), .cin(adder_1_cout), .cout(adder_2_cout));
  Adder #(.width(1)) adder_3 (.a(xor_3_out), .b(A[2]), .out(SUM_SUB[2]), .cin(adder_2_cout), .cout(adder_3_cout));
  Adder #(.width(1)) adder_4 (.a(xor_4_out), .b(A[3]), .out(SUM_SUB[3]), .cin(adder_3_cout), .cout(CARRYOUT));
endmodule
