// Logisim project COA LAB SEM 3.circ as structural Verilog: 13 circuits, main circuit main
module main (
  input  A,
  input  B,
  output SUM,
  output COUT
);

  xor xor_1 (SUM, A, B);
  and and_1 (COUT, A, B);
endmodule

module FULL_ADDER (
  input  A,
  input  B,
  input  CIN,
  output SUM,
  output COUT
);

  wire and_1_out, and_2_out, SUM_out, xor_1_out;

  xor xor_1 (xor_1_out, B, A);
  xor u_SUM (SUM_out, A, CIN);
  and and_1 (and_1_out, B, A);
  and and_2 (and_2_out, xor_1_out, CIN);
  xor SUM_2 (SUM, SUM_out, B);
  or u_COUT (COUT, and_2_out, and_1_out);
endmodule

module HALFSUBTRACTOR (
  input  A,
  input  B,
  output DIFFRENCE,
  output BOUT
);

  wire not_1_out;

  not not_1 (not_1_out, A);
  xor xor_1 (DIFFRENCE, B, A);
  and and_1 (BOUT, not_1_out, B);
endmodule

module FULLSUBTRACTOR (
  input  A,
  input  B,
  input  CIN,
  output SUB,
  output BOUT
);

  wire and_1_out, and_2_out, not_1_out, xnor_1_out, xor_1_out;

  not not_1 (not_1_out, A);
  xnor xnor_1 (xnor_1_out, A, B);
  and and_1 (and_1_out, not_1_out, B);
  xor xor_1 (xor_1_out, A, B);
  and and_2 (and_2_out, xnor_1_out, CIN);
  xor xor_2 (SUB, xor_1_out, CIN);
  or or_1 (BOUT, and_2_out, and_1_out);
endmodule

module FULLADDER_SUB (
  input  CIN,
  input  [3:0] A,
  input  [3:0] B,
  input  K,
  output S0,
  output S1,
  output S2,
  output S3,
  output COUT
);

  wire full_adder_1_cout, full_adder_2_cout, full_adder_3_cout, xor_1_out, xor_2_out, xor_3_out, xor_4_out;

  xor xor_1 (xor_1_out, B[0], K);
  xor xor_2 (xor_2_out, B[1], K);
  xor xor_3 (xor_3_out, B[2], K);
  xor xor_4 (xor_4_out, B[3], K);
  FULL_ADDER full_adder_1 (.A(A[0]), .B(xor_1_out), .CIN(CIN), .SUM(S0), .COUT(full_adder_1_cout));
  FULL_ADDER full_adder_2 (.A(A[1]), .B(xor_2_out), .CIN(full_adder_1_cout), .SUM(S1), .COUT(full_adder_2_cout));
  FULL_ADDER full_adder_3 (.A(A[2]), .B(xor_3_out), .CIN(full_adder_2_cout), .SUM(S2), .COUT(full_adder_3_cout));
  FULL_ADDER full_adder_4 (.A(A[3]), .B(xor_4_out), .CIN(full_adder_3_cout), .SUM(S3), .COUT(COUT));
endmodule

module ALF_FULLADDER_MUX (
  input  S1,
  input  S0,
  output SUM,
  output COUT
);

  _4X1MUX u_4x1mux_1 (.S1(S1), .S0(S0), .I0(1'b0), .I1(1'b1), .I2(1'b1), .I3(1'b0), .OUT(SUM));
  _4X1MUX u_4x1mux_2 (.S1(S1), .S0(S0), .I0(1'b0), .I1(1'b0), .I2(1'b0), .I3(1'b1), .OUT(COUT));
endmodule

module _4X1MUX (
  input  S1,
  input  S0,
  input  I0,
  input  I1,
  input  I2,
  input  I3,
  output OUT
);

  wire and_1_out, and_2_out, and_3_out, and_4_out, not_1_out, not_2_out, not_3_out, not_4_out;

  not not_1 (not_1_out, S1);
  not not_2 (not_2_out, S0);
  not not_3 (not_3_out, S1);
  not not_4 (not_4_out, S0);
  and and_1 (and_1_out, not_1_out, not_2_out, I0);
  and and_2 (and_2_out, not_3_out, I1, S0);
  and and_3 (and_3_out, S1, not_4_out, I2);
  and and_4 (and_4_out, S1, S0, I3);
  or or_1 (OUT, and_1_out, and_2_out, and_3_out, and_4_out);
endmodule

module _1BIT_ALU (
  input  A,
  input  CIN,
  input  B,
  input  S1,
  input  S0,
  output OUT,
  output COUT
);

  wire n4x1mux_1_out, not_1_out;

  not not_1 (not_1_out, B);
  _4X1MUX u_4x1mux_1 (.S1(S1), .S0(S0), .I0(B), .I1(not_1_out), .I2(1'b0), .I3(1'b1), .OUT(n4x1mux_1_out));
  FULL_ADDER full_adder_1 (.A(A), .B(n4x1mux_1_out), .CIN(CIN), .SUM(OUT), .COUT(COUT));
endmodule

module _4BITAU (
  input  CIN,
  input  [3:0] A,
  input  [3:0] B,
  input  [1:0] SELECT,
  output [3:0] out_5,
  output COUT
);

  wire n1bit_alu_1_cout, n1bit_alu_2_cout, n1bit_alu_3_cout;

  _1BIT_ALU u_1bit_alu_1 (
    .A(A[0]), .CIN(CIN), .B(B[0]), .S1(SELECT[1]), .S0(SELECT[0]), .OUT(out_5[0]), .COUT(n1bit_alu_1_cout));
  _1BIT_ALU u_1bit_alu_2 (
    .A(A[1]), .CIN(n1bit_alu_1_cout), .B(B[1]), .S1(SELECT[1]), .S0(SELECT[0]), .OUT(out_5[1]),
    .COUT(n1bit_alu_2_cout));
  _1BIT_ALU u_1bit_alu_3 (
    .A(A[2]), .CIN(n1bit_alu_2_cout), .B(B[2]), .S1(SELECT[1]), .S0(SELECT[0]), .OUT(out_5[2]),
    .COUT(n1bit_alu_3_cout));
  _1BIT_ALU u_1bit_alu_4 (
    .A(A[3]), .CIN(n1bit_alu_3_cout), .B(B[3]), .S1(SELECT[1]), .S0(SELECT[0]), .OUT(out_5[3]), .COUT(COUT));
endmodule

module LU (
  input  [3:0] A,
  input  [3:0] B,
  input  [1:0] SELECT,
  output [3:0] out_4
);

  wire [3:0] and_1_out, not_1_out, or_1_out, xor_1_out;

  assign and_1_out = B & A;  // AND_Gate and_1, 4 bits wide
  assign or_1_out = B | A;  // OR_Gate or_1, 4 bits wide
  assign xor_1_out = B ^ A;  // XOR_Gate xor_1, 4 bits wide
  assign not_1_out = ~A;  // NOT_Gate not_1, 4 bits wide
  Multiplexer #(.select(2), .width(4), .enable("false")) multiplexer_1 (
    .in0(and_1_out), .in1(or_1_out), .in2(xor_1_out), .in3(not_1_out), .out(out_4), .sel(SELECT));
endmodule

// ALU
module _4BITALU (
  input  CIN,
  input  [3:0] A,
  input  [3:0] B,
  input  [1:0] SELECT,
  input  LU_AU,
  output [3:0] OUTPUT,
  output COUT
);

  wire [3:0] lu_1_out_4, n4bitau_1_out_5;

  _4BITAU u_4bitau_1 (.CIN(CIN), .A(A), .B(B), .SELECT(SELECT), .out_5(n4bitau_1_out_5), .COUT(COUT));
  LU lu_1 (.A(A), .B(B), .SELECT(SELECT), .out_4(lu_1_out_4));
  Multiplexer #(.width(4), .enable("false")) multiplexer_1 (
    .in0(n4bitau_1_out_5), .in1(lu_1_out_4), .out(OUTPUT), .sel(LU_AU));
endmodule

module REGISTERREAD_WRITE (
  input  [1:0] REGISTERSELECT,
  input  [3:0] A,
  input  [1:0] READ_REGISTER_SELECT0,
  input  [1:0] READ_REGISTER_SELECT1,
  output [3:0] OUT1,
  output [3:0] OUT2
);

  wire clock_1_out, decoder_1_out0, decoder_1_out1, decoder_1_out2, decoder_1_out3;
  wire [3:0] register_1_q, register_2_q, register_3_q, register_4_q;

  Decoder #(.select(2), .enable("false")) decoder_1 (
    .out0(decoder_1_out0), .out1(decoder_1_out1), .out2(decoder_1_out2), .out3(decoder_1_out3),
    .sel(REGISTERSELECT));
  Clock clock_1 (.out(clock_1_out));
  Register #(.width(4)) register_1 (.D(A), .en(decoder_1_out0), .Q(register_1_q), .clk(clock_1_out));  // open: clr
  Register #(.width(4)) register_2 (.D(A), .en(decoder_1_out1), .Q(register_2_q), .clk(clock_1_out));  // open: clr
  Register #(.width(4)) register_3 (.D(A), .en(decoder_1_out2), .Q(register_3_q), .clk(clock_1_out));  // open: clr
  Register #(.width(4)) register_4 (.D(A), .en(decoder_1_out3), .Q(register_4_q), .clk(clock_1_out));  // open: clr
  Multiplexer #(.select(2), .width(4), .enable("false")) multiplexer_1 (
    .in0(register_1_q), .in1(register_2_q), .in2(register_3_q), .in3(register_4_q), .out(OUT1),
    .sel(READ_REGISTER_SELECT0));
  Multiplexer #(.select(2), .width(4), .enable("false")) multiplexer_2 (
    .in0(register_1_q), .in1(register_2_q), .in2(register_3_q), .in3(register_4_q), .out(OUT2),
    .sel(READ_REGISTER_SELECT1));
endmodule

module ALU_REGISTER_FILE (
  input  CIN,
  input  [1:0] REGISTERSELECT,
  input  [3:0] A,
  input  [1:0] OP_SELECT,
  input  LU_AU,
  input  [1:0] READ_REGISTER_SELECT0,
  input  [1:0] READ_REGISTER_SELECT1,
  output [3:0] OUT,
  output COUT
);

  wire clock_1_out, decoder_1_out0, decoder_1_out1, decoder_1_out2, decoder_1_out3;
  wire [3:0] multiplexer_1_out, multiplexer_2_out, register_1_q, register_2_q, register_3_q, register_4_q;

  Decoder #(.select(2), .enable("false")) decoder_1 (
    .out0(decoder_1_out0), .out1(decoder_1_out1), .out2(decoder_1_out2), .out3(decoder_1_out3),
    .sel(REGISTERSELECT));
  Clock clock_1 (.out(clock_1_out));
  Register #(.width(4)) register_1 (.D(A), .en(decoder_1_out0), .Q(register_1_q), .clk(clock_1_out));  // open: clr
  Register #(.width(4)) register_2 (.D(A), .en(decoder_1_out1), .Q(register_2_q), .clk(clock_1_out));  // open: clr
  Register #(.width(4)) register_3 (.D(A), .en(decoder_1_out2), .Q(register_3_q), .clk(clock_1_out));  // open: clr
  Register #(.width(4)) register_4 (.D(A), .en(decoder_1_out3), .Q(register_4_q), .clk(clock_1_out));  // open: clr
  Multiplexer #(.select(2), .width(4), .enable("false")) multiplexer_1 (
    .in0(register_1_q), .in1(register_2_q), .in2(register_3_q), .in3(register_4_q), .out(multiplexer_1_out),
    .sel(READ_REGISTER_SELECT0));
  Multiplexer #(.select(2), .width(4), .enable("false")) multiplexer_2 (
    .in0(register_1_q), .in1(register_2_q), .in2(register_3_q), .in3(register_4_q), .out(multiplexer_2_out),
    .sel(READ_REGISTER_SELECT1));
  _4BITALU u_4bitalu_1 (
    .CIN(CIN), .A(multiplexer_1_out), .B(multiplexer_2_out), .SELECT(OP_SELECT), .LU_AU(LU_AU), .OUTPUT(OUT),
    .COUT(COUT));
endmodule
